# Fritzing sketch sketch (saved by Fritzing 1.0.2b)

parts:
  Part1 = Adafruit 1.54" Tri-Color eInk / ePaper Display with SRAM [part_number=3625]
  M2 = ESP32-C3-DevKitM-1 [part_number=ESP32-C3-DevKitM-1]
  Mod1 = CJMCU-811
  R1 = Resistor [tolerance=±5% resistance=4.7k package="0402 [SMD]"]
  R2 = Resistor [tolerance=±5% resistance=4.7k package="0402 [SMD]"]
  R3 = Resistor [tolerance=±5% resistance=4.7k package="0402 [SMD]"]

nets:
  GND: Part1.GND, M2.GND-1, M2.GND-15, M2.GND-30, Mod1.GND
  N1: Part1.SCLK, M2.6
  N2: Part1.MISO, M2.7
  N3: Part1.MOSI, Part1.DISPCS, M2.8
  N4: Part1.DC, M2.19
  N5: Part1.SDCS, Part1.RESET, M2.10
  N6: Part1.BUSY, M2.9
  N7: M2.3V3-17, Mod1.VCC, R3.Pin_1
  N8: M2.2, Mod1.SDA, R2.Pin_0
  N9: M2.3, Mod1.SCL, R3.Pin_0
  N10: Mod1.WAK, R1.Pin_0
  N11: Mod1.RST, R1.Pin_1

custom parts:
  Adafruit 1.54" Tri-Color eInk / ePaper Display with SRAM: This small 1.54" tri-color display has 152x152 black and red ink pixels and a white-ish background. Using our Arduino library, you can create a 'frame buffer' with what pixels you want to have activated and then write that out to the display. We tossed a small SRAM chip on the back. This chip shares the SPI port the eInk display uses, so you only need one extra pin. And, no more frame-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
  ESP32-C3-DevKitM-1: Espressif Esp32 DevKit v1 is one of the development board created by DOIT to evaluate the ESP-WROOM-32 module. It is based on the ESP32 microcontroller that boasts Wifi, Bluetooth, Ethernet and Low Power support all in a single chip. (vanepp) Feb 2021: converted to ESP32-C3-DevKitM-1. This chip is 30pins long (2 x15) and 11 pins width.
  CJMCU-811: The CCS811 is an ultra-low power digital gas sensor solution which integrates a metal oxide (MOX) gas sensor to detect a wide range of Volatile Organic Compounds (VOCs) for indoor air quality monitoring with a microcontroller unit (MCU), which includes an Analog-to-Digital converter (ADC), and an I²C interface.
